# Fritzing sketch schematic (saved by Fritzing 0.9.3b)
breadboards: 1

parts:
  WeMos_D1_Mini1 = WeMos D1 Mini
  Mod1 = MQ-7 breakout

nets:
  5V: WeMos_D1_Mini1.5V, Mod1.VCC
  N1: WeMos_D1_Mini1.A0, Mod1.GND
  N2: WeMos_D1_Mini1.G, Mod1.AO

custom parts:
  MQ-7 breakout: MQ-5 gas sensor
